# Fritzing sketch esp8266 WebServer final MEGA (saved by Fritzing 0.9.2b)
breadboards: 1

parts:
  Part1 = Breadboard Power Supply Board SMD
  Part2 = Arduino Mega 2560 (Rev3)
  Espessif_Serial_Wifi_Modul_1 = ESP8266 ESP01 [part_number=ESP8266 package=THT]
  R1 = Resistor [tolerance=±5% resistance=1k package=THT]
  R2 = Resistor [tolerance=±5% resistance=2.2k package=THT]
  S1 = Pushbutton [package="[THT]"]
  S2 = Pushbutton [package="[THT]"]
  R4 = Resistor [tolerance=±2% resistance=10k package=THT]
  R5 = Resistor [tolerance=±2% resistance=10k package=THT]
  R7 = Rotary Potentiometer (Small) [maximum_resistance=100kΩ package=THT]

nets:
  GND: Part1.GND, Part2.GND, Espessif_Serial_Wifi_Modul_1.GND, R2.Pin_1, R4.Pin_1, R5.Pin_1, R7.leg2
  VCC: Part1.VCC, Part2.D8_PWM, Espessif_Serial_Wifi_Modul_1.VCC, Espessif_Serial_Wifi_Modul_1.GPIO16, S1.Pin_1, S1.Pin_2, S2.Pin_1, S2.Pin_2
  N1: Part2.A0, R7.wiper
  N2: Part2.D17_PWM/RX2, Espessif_Serial_Wifi_Modul_1.TXD
  N3: Part2.D16_PWM/TX2, R1.Pin_0
  N4: Part2.D9_PWM, S1.Pin_3, S1.Pin_4, R4.Pin_0
  N5: Part2.5V, R7.leg1
  N6: Part2.D4_PWM, Espessif_Serial_Wifi_Modul_1.CH_PD
  N7: S2.Pin_3, S2.Pin_4, R5.Pin_0

custom parts:
  ESP8266 ESP01: Generic WiFi Module based on the ESP8266 with onboard PCB antenna and UART communications

// code stored in the sketch: esp8266 test.ino
/*************************************************************************
* Web Server with ESP8266
* Based on: FILIPEFLOP http://blog.filipeflop.com/wireless/esp8266-arduino-tutorial.html
* Adapted by Marcelo Jose Rovai
**************************************************************************/

#define esp8266 Serial2
#define CH_PD 4 
#define speed8266 115200 // This is the speed that worked with my ESP8266
 
#define DEBUG true
 
void setup()
{
  esp8266.begin (speed8266); 
  Serial.begin(9600);
  reset8266(); // Pin CH_PD needs a reset before start communication
  InitWifiModule() // Inciate module as WebServer 
}
 
void loop()
{
  if (esp8266.available()) // check if 8266 is sending data
  {
    if (esp8266.find("+IPD,"))
    {
      delay(300);
      int connectionId = esp8266.read() - 48;
 
      String webpage = "<head><meta http-equiv=""refresh"" content=""3"">";
      webpage += "</head><h1>MJRoBot WebServer ESP8266</h1><h2>Arduino Pin: ";
      webpage += "D8 status ==> ";
      int a = digitalRead(8);
      webpage += a;
      webpage += "<h2>Arduino Pin: D9 status ==> ";
      int b = digitalRead(9);
      webpage += b;
      webpage += "<h2>Arduino Pin: A0 data ===> ";
      int c = analogRead(0);
      webpage += c;
      webpage += "</h2>";
      
      String cipSend = "AT+CIPSEND=";
      cipSend += connectionId;
      cipSend += ",";
      cipSend += webpage.length();
      cipSend += "\r\n";
 
      sendData(cipSend, 1000, DEBUG);
      sendData(webpage, 1000, DEBUG);
 
      String closeCommand = "AT+CIPCLOSE=";
      closeCommand += connectionId; // append connection id
      closeCommand += "\r\n";
 
      sendData(closeCommand, 3000, DEBUG);
    }
  }
}
 
/*************************************************/
void InitWifiModule()
{
  sendData("AT+RST\r\n", 2000, DEBUG); // reset
  sendData("AT+CWJAP=\"ROVAI TIMECAP\",\"mjr747@1\"\r\n", 2000, DEBUG); //Connect network
  delay(3000);
  sendData("AT+CWMODE=1\r\n", 1000, DEBUG);
  sendData("AT+CIFSR\r\n", 1000, DEBUG); // Show IP Adress
  sendData("AT+CIPMUX=1\r\n", 1000, DEBUG); // Multiple conexions
  sendData("AT+CIPSERVER=1,80\r\n", 1000, DEBUG); // start comm port 80
}

/*************************************************/ 
 // Send AT commands to module
String sendData(String command, const int timeout, boolean debug)
{
  String response = "";
  esp8266.print(command);
  long int time = millis();
  while ( (time + timeout) > millis())
  {
    while (esp8266.available())
    {
      // The esp has data so display its output to the serial window
      char c = esp8266.read(); // read the next character.
      response += c;
    }
  }
  if (debug)
  {
    Serial.print(response);
  }
  return response;
}

/*************************************************/
// Reset funtion to accept communication
void reset8266 ()
{
  pinMode(CH_PD, OUTPUT);
  digitalWrite(CH_PD, LOW);
  delay(300);
  digitalWrite(CH_PD, HIGH);
}
