# Fritzing sketch ES8266_Arduino_UNO_GPIO_Control (saved by Fritzing 0.9.2b)
breadboards: 1

parts:
  Part1 = Breadboard Power Supply Board SMD
  Espessif_Serial_Wifi_Modul_1 = ESP8266 ESP01 [part_number=ESP8266 package=THT]
  R1 = Resistor [tolerance=±5% resistance=1k package=THT]
  R2 = Resistor [tolerance=±5% resistance=2.2k package=THT]
  Part2 = Arduino Uno (Rev3)
  LED1 = smd LED [color="Green (555nm)" package="1206 [SMD]"]
  LED2 = smd LED [color="Red (633nm)" package="1206 [SMD]"]
  LED3 = smd LED [color="Blue (470nm)" package="1206 [SMD]"]

nets:
  GND: Part1.GND, Espessif_Serial_Wifi_Modul_1.GND, R2.Pin_1, Part2.GND, LED1.cathode, LED2.cathode, LED3.cathode
  VCC: Part1.VCC, Espessif_Serial_Wifi_Modul_1.VCC, Espessif_Serial_Wifi_Modul_1.GPIO16
  N1: Espessif_Serial_Wifi_Modul_1.RXD, R1.Pin_1, R2.Pin_0
  N2: Espessif_Serial_Wifi_Modul_1.TXD, Part2.D2
  N3: Espessif_Serial_Wifi_Modul_1.CH_PD, Part2.D4
  N4: R1.Pin_0, Part2.D3_PWM
  N5: Part2.D11_PWM/MOSI, LED3.anode
  N6: Part2.D12/MISO, LED2.anode
  N7: Part2.D13/SCK, LED1.anode

custom parts:
  ESP8266 ESP01: Generic WiFi Module based on the ESP8266 with onboard PCB antenna and UART communications

// code stored in the sketch: esp8266 test.ino
/**************************************************************************************************
* ES8266 Arduino Uno GPIO Control
* LED ON/OFF
* Sketch adaptada do original https://youtu.be/xa6dJvd7wHg?list=PLbADmeIeQARotrEv9bTuOVyJLOYOD-pPM
*
* Marcelo Jose Rovai - 19Jan2016
***************************************************************************************************/

//#define esp8266 Serial2 <===== In case of using MEGA, take out the comment
#include <SoftwareSerial.h>   // In case of using MEGA, mark the line as comment
SoftwareSerial esp8266(2,3);  // In case of using MEGA, mark the line as comment
//Rx ==> Pin 2; TX ==> Pin3 

#define speed8266 9600  // <========= Change the Speed for the one used at Module
#define CH_PD 4 
#define DEBUG true

int red =12;
int green =13;
int blue =11;


void setup()

{
  pinMode(red,OUTPUT);
  pinMode(green,OUTPUT);
  pinMode(blue,OUTPUT);
  
  digitalWrite(red,LOW);
  digitalWrite(green,LOW);
  digitalWrite(blue,HIGH);

  Serial.begin(9600);
  esp8266.begin(speed8266);

  reset8266(); 
  InitWifiModule();

  digitalWrite(blue,LOW);
  digitalWrite(green,HIGH);
  delay(2000);
  digitalWrite(green,LOW);
}

void loop()
{

  if(esp8266.available())
  {
    if(esp8266.find("+IPD,"))
    {
      delay(1000);  
      int connectionId = esp8266.read()-48;  
      esp8266.find("pin="); 
      int pinNumber = (esp8266.read()-48)*10; 
      pinNumber += (esp8266.read()-48); 
      int statusLed =(esp8266.read()-48);

      digitalWrite(pinNumber, statusLed);

      String closeCommand = "AT+CIPCLOSE="; 
      closeCommand+=connectionId; 
      closeCommand+="\r\n";
      sendData(closeCommand,1000,DEBUG); 
    }
  }
}

/*****************************************************************************************
* Name: sendData
* Description: Function used to send data to ESP8266.
* Params: command - the data/command to send; timeout - the time to wait for a response; debug - print to Serial window?(true = yes, false = no)
* Returns: The response from the esp8266 (if there is a reponse)
*/
String sendData(String command, const int timeout, boolean debug)
{
    String response = "";
    
    esp8266.print(command); // send the read character to the esp8266
    long int time = millis();
    while( (time+timeout) > millis())
    {
      while(esp8266.available())
      {
        char c = esp8266.read(); // read the next character.
        response+=c;
      }  
    }
    
    if(debug)
    {
      Serial.print(response);
    }    
    return response;
}




/***********************************************************************/  
// This initializes the Wifi Module as a server 
void InitWifiModule()
{
  sendData("AT+RST\r\n", 2000, DEBUG); // reset
  sendData("AT+CWMODE=1\r\n", 1000, DEBUG);
  //sendData("AT+CWJAP=\"XXXXXXXXXXX\",\"YYYYYYYY\"\r\n", 2000, DEBUG); //Connect network
  delay (1000);
  sendData("AT+CIFSR\r\n", 1000, DEBUG); // Show IP Adress
  sendData("AT+CIPMUX=1\r\n", 1000, DEBUG); // Multiple conexions
  sendData("AT+CIPSERVER=1,80\r\n", 1000, DEBUG); // start comm port 80
}

/*************************************************/
// Reset funtion to accept communication
void reset8266 ()
{
  pinMode(CH_PD, OUTPUT);
  digitalWrite(CH_PD, LOW);
  delay(300);
  digitalWrite(CH_PD, HIGH);
}
